# Fritzing sketch CoffeeMaker_NodeMCU (saved by Fritzing 0.9.3b)
breadboards: 1

parts:
  BLE_HC-05 = Bluetooth HC-05 Macho
  NodeMCU_Amica = NodeMCU V1.0
  Buzzer = Piezo Speaker
  Display = OLED 0.96" 128x64 I2C SSD1306
  NFC_Reader = Adafruit PN532 Breakout [part_number="Adafruit #364"]
  D-SUB9 = DB9 Connector [package=db9]

nets:
  N1: BLE_HC-05.TXD, NodeMCU_Amica.RX
  N2: BLE_HC-05.RXD, NodeMCU_Amica.TX
  VCC: BLE_HC-05.VCC, NodeMCU_Amica.3V3, Display.VCC, NFC_Reader.VDD
  GND: BLE_HC-05.GND, NodeMCU_Amica.GND, Buzzer.pin2, Display.GND, NFC_Reader.GND, D-SUB9.2
  N3: NodeMCU_Amica.D1, Display.SCL
  N4: NodeMCU_Amica.D2, Display.SCA
  N5: NodeMCU_Amica.D3, Buzzer.pin1
  N6: NodeMCU_Amica.D5, NFC_Reader.SCK
  N7: NodeMCU_Amica.D6, NFC_Reader.MISO
  N8: NodeMCU_Amica.D7, NFC_Reader.MOSI/SDA/TX
  N9: NodeMCU_Amica.D8, NFC_Reader.NSS/SCL/RX
  N10: NodeMCU_Amica.SD2, D-SUB9.1
  N11: NodeMCU_Amica.SD3, D-SUB9.3

custom parts:
  NodeMCU V1.0: ESP8266 based NodeMCU
  Adafruit PN532 Breakout: The PN532 is the most popular NFC chip, and is what is embedded in pretty much every phone or device that does NFC. It can pretty much do it all, such as read and write to tags and cards, communicate with phones (say for payment processing), and 'act' like a NFC tag. If you want to do any sort of embedded NFC work, this is the chip you'll want to use! NFC (Near Field Communications) is a way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
