# Fritzing sketch CoffeeMaker_SparkFun_ESP32_V1 (saved by Fritzing 0.9.3b)
circuit board: 9.2cm x 7.5cm
breadboards: 1

parts:
  SparkFun_ESP32_Thing1 = SparkFun ESP32 Thing [part_number=DEV-13907]
  Oled_SPI_Header = female pin header, 8 pins [form="♀ (female)"]
  PN532_NFC = female pin header, 9 pins [form="♀ (female)"]
  Buzzer = Header 2 [package=jst-2-pth-ns]
  MicroUSBConnector = Adafruit Micro USB Breakout [part_number="Adafruit #1833"]
  RC522_RFID = female pin header, 8 pins [form="♀ (female)"]
  TFT_SPI_Header = female pin header, 8 pins [form="♀ (female)"]

nets:
  GND: SparkFun_ESP32_Thing1.GND, Oled_SPI_Header.pin2, PN532_NFC.pin2, Buzzer.1, MicroUSBConnector.GND, RC522_RFID.pin6, TFT_SPI_Header.pin7
  N1: SparkFun_ESP32_Thing1.3.3V, Oled_SPI_Header.pin1, PN532_NFC.pin1, RC522_RFID.pin8, TFT_SPI_Header.pin1, TFT_SPI_Header.pin8
  N2: SparkFun_ESP32_Thing1.V_BATT, MicroUSBConnector.VBUS
  N3: SparkFun_ESP32_Thing1.16, MicroUSBConnector.D-
  N4: SparkFun_ESP32_Thing1.17, MicroUSBConnector.D+
  N5: SparkFun_ESP32_Thing1.2, PN532_NFC.pin4, RC522_RFID.pin1
  N6: SparkFun_ESP32_Thing1.15, Oled_SPI_Header.pin7, TFT_SPI_Header.pin4
  N7: SparkFun_ESP32_Thing1.5, Oled_SPI_Header.pin6, TFT_SPI_Header.pin6
  N8: SparkFun_ESP32_Thing1.18, Oled_SPI_Header.pin5, PN532_NFC.pin7, RC522_RFID.pin2, TFT_SPI_Header.pin2
  N9: SparkFun_ESP32_Thing1.23, Oled_SPI_Header.pin4, PN532_NFC.pin5, RC522_RFID.pin3, TFT_SPI_Header.pin3
  N10: SparkFun_ESP32_Thing1.19, PN532_NFC.pin6, RC522_RFID.pin4
  N11: SparkFun_ESP32_Thing1.22, TFT_SPI_Header.pin5
  N12: SparkFun_ESP32_Thing1.21, Buzzer.2

notes:
  3,3V
  GND
  DIN
  CLK
  CS
  DC
  RST
  NC
  IRQ
  SCL
  MOSI
  MISO
  SCK
  RSTOUT
  5V
  TX
  RX
  +
  www.thank-the-maker.org
  SDA
  LED
  A0
  RESET
  VCC

custom parts:
  SparkFun ESP32 Thing: The SparkFun ESP32 Thing is a comprehensive development platform for Espressif’s ESP32, their super-charged version of the popular ESP8266. Like the 8266, the ESP32 is a WiFi-compatible microcontroller, but to that it adds support for Bluetooth low-energy (i.e BLE, BT4.0, Bluetooth Smart), and nearly 30 I/O pins. The ESP32’s power and versatility will make it the foundation of IoT and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
  Adafruit Micro USB Breakout: Simple but effective - this breakout board has a USB Micro-B connector, with all 5 pins broken out. Great for pairing with a microcontroller with USB support, or adding USB 5V power to a project. We use a micro-AB connector with through-hole shielding pads for an excellent strong connection - it won't rip off by accident! Comes with one fully assembled and tested micro B breakout PCB and a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
