# Fritzing sketch CoffeeMaker_Sparkfun (saved by Fritzing 0.9.3b)

parts:
  Bauteil1 = SparkFun ESP8266 Thing
  Bauteil2 = Bluetooth HC-05 Macho
  X1 = DB9 Connector [package=db9]
  J1 = Piezo Speaker
  Squix1 = OLED 0.96" 128x64 I2C SSD1306
  Bauteil3 = Adafruit PN532 Breakout [part_number="Adafruit #364"]

nets:
  GND: Bauteil1.GND, Bauteil2.GND, X1.2, J1.pin2, Squix1.GND, Bauteil3.GND
  VCC: Bauteil1.VCC, Bauteil2.VCC, Squix1.VCC
  N1: Bauteil1.GPIO2, Bauteil3.NSS/SCL/RX
  N2: Bauteil1.GPIO14, Bauteil3.SCK
  N3: Bauteil1.U0TXO, Bauteil2.TXD
  N4: Bauteil1.U0RXI, Bauteil2.RXD
  N5: Bauteil1.USBVCC, Bauteil3.+5.0V
  N6: Bauteil1.GPIO5, Squix1.SCL
  N7: Bauteil1.GPIO0, J1.pin1
  N8: Bauteil1.GPIO4, Squix1.SCA
  N9: Bauteil1.GPIO13, Bauteil3.MOSI/SDA/TX
  N10: Bauteil1.GPIO12, Bauteil3.MISO
  N11: Bauteil1.GPIO16, X1.3
  N12: Bauteil1.GPIO15, X1.1

custom parts:
  Adafruit PN532 Breakout: The PN532 is the most popular NFC chip, and is what is embedded in pretty much every phone or device that does NFC. It can pretty much do it all, such as read and write to tags and cards, communicate with phones (say for payment processing), and 'act' like a NFC tag. If you want to do any sort of embedded NFC work, this is the chip you'll want to use! NFC (Near Field Communications) is a way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
