# Fritzing sketch Coffeemaker_NodeMCU_TFT_RC522 (saved by Fritzing 0.9.3b)

parts:
  Bauteil1 = TFT 1.8 inch 160x128 w microSD [part_number=358]
  U1 = NodeMCU V1.0
  Bauteil2 = RFID-RC522-v3
  J1 = Piezo Speaker
  X1 = DB9 Connector [package=db9]

nets:
  N1: Bauteil1.MISO, U1.D6, Bauteil2.MISO
  N2: Bauteil1.SCLK, U1.D5, Bauteil2.SCK
  N3: Bauteil1.MOSI, U1.D7, Bauteil2.MOSI
  N4: Bauteil1.TFTCS, U1.D1
  N5: Bauteil1.CARDCS, U1.D8
  N6: Bauteil1.TFTDC, U1.D3
  N7: Bauteil1.RESET, U1.D2
  +5V: Bauteil1.+5V, U1.3V3, Bauteil2.3.3V
  GND: Bauteil1.GND, U1.GND, J1.pin2, X1.2
  N8: U1.D0, X1.1
  N9: U1.D4, X1.3
  N10: U1.RX, J1.pin1
  N11: U1.SD2, Bauteil2.SDA
  N12: U1.SD3, Bauteil2.RST

custom parts:
  TFT 1.8 inch 160x128 w microSD: This lovely little display breakout is the best way to add a small, colorful and bright display to any project. Since the display uses 4-wire SPI to communicate and has its own pixel-addressable frame buffer, it can be used with every kind of microcontroller. Even a very small one with low memory and few pins available! The 1.8" display has 128x160 color pixels.
  NodeMCU V1.0: ESP8266 based NodeMCU
  RFID-RC522-v3: A simple China made RFID-RC522 Reader (6x4 cm); do check the pin labels, as this is a MFRC522 based clone.
